// Logisim project CPU_design.circ as structural Verilog: 1 circuit, main circuit main
module main (
);

  wire and_1_out, and_2_out, and_3_out, clock_1_out, not_1_out, not_2_out, not_3_out, not_4_out, not_5_out,
       or_1_out, or_2_out, or_3_out, or_4_out;
  wire [3:0] controlled_buffer_1_out, controlled_buffer_1_out_2;
  wire [6:0] keyboard_1_data;
  wire [7:0] counter_1_q, register_1_q, register_2_q;
  wire [11:0] rom_1_data;

  not not_1 (not_1_out, or_1_out);
  Counter counter_1 (
    .load(or_1_out), .D({controlled_buffer_1_out_2, controlled_buffer_1_out}), .count(not_1_out),
    .Q(counter_1_q), .clk(clock_1_out));  // open: carry, clr
  ROM #(.dataWidth(12)) rom_1 (.addr(counter_1_q), .data(rom_1_data), .sel(1'b1));
  not not_2 (not_2_out, rom_1_data[11]);
  not not_3 (not_3_out, rom_1_data[8]);
  not not_4 (not_4_out, rom_1_data[9]);
  not not_5 (not_5_out, rom_1_data[10]);
  and and_1 (and_1_out, not_3_out, not_4_out, not_5_out, not_2_out);
  and and_2 (and_2_out, rom_1_data[8], not_4_out, not_5_out, not_2_out);
  and and_3 (and_3_out, not_3_out, rom_1_data[9], not_5_out, not_2_out);
  Clock clock_1 (.out(clock_1_out));
  assign {controlled_buffer_1_out_2, controlled_buffer_1_out} = or_2_out ? rom_1_data[7:0] : 8'bz;  // Controlled_Buffer controlled_buffer_1
  buf or_1 (or_1_out, and_3_out);  // OR_Gate
  or or_2 (or_2_out, and_1_out, and_2_out, and_3_out);
  buf or_3 (or_3_out, and_1_out);  // OR_Gate
  Register register_1 (
    .D({controlled_buffer_1_out_2, controlled_buffer_1_out}), .en(or_3_out), .Q(register_1_q),
    .clk(clock_1_out));  // open: clr
  buf or_4 (or_4_out, and_2_out);  // OR_Gate
  Register register_2 (
    .D({controlled_buffer_1_out_2, controlled_buffer_1_out}), .en(or_4_out), .Q(register_2_q),
    .clk(clock_1_out));  // open: clr
  TTY tty_1 (.data(register_1_q[6:0]), .clk(clock_1_out), .we(register_2_q[1]));  // open: clr
  Keyboard keyboard_1 (.clk(clock_1_out), .re(register_2_q[0]), .data(keyboard_1_data));  // open: clr, avail
  assign {controlled_buffer_1_out_2, controlled_buffer_1_out} = 1'b0 ? {1'b0, keyboard_1_data} : 8'bz;  // Controlled_Buffer controlled_buffer_2
  Hex_Digit_Display hex_digit_display_1 (.value(controlled_buffer_1_out_2));  // open: dp
  Hex_Digit_Display hex_digit_display_2 (.value(controlled_buffer_1_out));  // open: dp

  // Notes on the sheet:
  //   IP
  //   Program Memory
  //   contents of rom_1 (hex, n*v repeats v):
  //   102 4d 61 72 61 20 64 61 6a 20 64 65 63 6b 69 6d 61 20 64 6f 6e 65 73 69 20 6a 6f 73 20 6a 65 64 6e
  //   75 20 72 75 6e 64 75 20 6b 61 72 6c 6f 76 61 63 6b 6f 67 a a 100 200
  //   BUS to IP
  //   Literal to BUS
  //   Set IO1 TTY
  //   Set IO2 Enable TTY (2) & KEY (1)
  //   8bit DATA BUS
  //   KEYB to BUS
endmodule
